# Fritzing sketch wiring (saved by Fritzing 0.9.4)
breadboards: 1

parts:
  Part1 = Arduino Nano (Rev3.0)
  J1 = Power Jack [package=power_jack_pth_lock]
  J2 = female pin header, 10 pins [form="♀ (female)"]
  J3 = female pin header, 3 pins [form="♀ (female)"]

nets:
  GND: Part1.GND, J1.GND, J2.pin2, J3.pin3
  N1: Part1.D5, J2.pin10
  N2: Part1.D6, J2.pin9
  N3: Part1.D7, J2.pin8
  N4: Part1.D8, J2.pin7
  N5: Part1.D9, J2.pin6
  N6: Part1.D10, J2.pin5
  N7: Part1.D11/MOSI, J2.pin4
  N8: Part1.D12/MISO, J2.pin3
  N9: Part1.VIN, J1.PWR, J3.pin1
  N10: Part1.5V, J2.pin1
